# Fritzing sketch final_creative_embedded_sys_fritzingdiagram (saved by Fritzing 1.0.4)
breadboards: 1

parts:
  Mod1 = ESP32-TTGO-T-DISPLAY
  R1 = Slide Potentiometer [maximum_resistance=10kΩ knob_status=50% power=0.5W package=THT]
  R2 = Slide Potentiometer [maximum_resistance=10kΩ knob_status=50% power=0.5W package=THT]
  R3 = Rotary Potentiometer (Small) [maximum_resistance=10kΩ knob_status=50% power=0.5W package=THT]
  R4 = Rotary Potentiometer (Small) [maximum_resistance=10kΩ knob_status=50% power=0.5W package=THT]

nets:
  N1: Mod1.G-1, Mod1.G-2, Mod1.G-10, Mod1.G-11, Mod1.G-14, R1.leg1, R2.leg1, R3.leg1, R4.leg1
  N2: Mod1.22, R3.wiper
  N3: Mod1.2, R1.wiper
  N4: Mod1.39, R2.wiper
  N5: Mod1.38, R4.wiper
  N6: R1.leg2, R2.leg2, R3.leg2, R4.leg2

custom parts:
  ESP32-TTGO-T-DISPLAY: LILYGO TTGO T-Display GD32VF103CBT6 Main Chip ST7789 1.14 Inch IPS 240x135 Resolution Minimalist Development Board.
